# Fritzing sketch exercise-2 (saved by Fritzing 0.9.6b)
breadboards: 1

parts:
  R1 = Resistor [tolerance=±5% power=0.25 resistance=330 package=THT]
  LED1 = LED - 5mm [color="Red (633nm)" current=0.030 package="5 mm [THT]"]
  S1 = Pushbutton [package="[THT]"]
  S2 = Pushbutton [package="[THT]"]
  Raspberry_Pi_1 = Raspberry Pi 3 [part_number=RPI-3-V1.2]
  R2 = Resistor [tolerance=±5% power=0.25 resistance=330 package=THT]

nets:
  N1: R1.Pin_0, LED1.anode
  N2: R1.Pin_1, Raspberry_Pi_1.GIPO16
  N3: LED1.cathode, Raspberry_Pi_1.GND
  N4: S1.Pin_1, S1.Pin_2, Raspberry_Pi_1.GIPO14
  N5: S1.Pin_3, S1.Pin_4, S2.Pin_3, S2.Pin_4, R2.Pin_0
  N6: S2.Pin_1, S2.Pin_2, Raspberry_Pi_1.GIPO15
  N7: Raspberry_Pi_1.3v3, R2.Pin_1
