# Fritzing sketch exercise-5 (saved by Fritzing 0.9.6b)
breadboards: 1

parts:
  Raspberry_Pi_1 = Raspberry Pi 3 [part_number=RPI-3-V1.2]
  R1 = PHOTOCELL [package=photocell]
  R2 = Resistor [tolerance=±5% resistance=10k package="0402 [SMD]"]
  R3 = Resistor [tolerance=±5% resistance=220 package="0402 [SMD]"]
  LED1 = LED - 5mm [color="Red (633nm)" current=0.030 package="5 mm [THT]"]

nets:
  N1: Raspberry_Pi_1.3v3, R1.P$1
  N2: Raspberry_Pi_1.GIPO25, R3.Pin_0
  N3: Raspberry_Pi_1.GND, R2.Pin_1, LED1.cathode
  N4: Raspberry_Pi_1.GIPO24, R1.P$2, R2.Pin_0
  N5: R3.Pin_1, LED1.anode
